# Fritzing sketch PlantManagerDevice (saved by Fritzing 0.9.3b)
breadboards: 1

parts:
  Part1 = Arduino Pro Mini v13
  U2 = V_REG_LD1117VXX [package=78xxl]
  V1 = DC Power [voltage=12V]
  U3 = ESP8266 WiFi Module [part_number=ESP8266]
  C1 = Capacitor Polarized [package=panasonic_g]
  C2 = Capacitor [package=cap-pth-small2]
  C3 = Capacitor Polarized [package=panasonic_g]
  C4 = Capacitor [package=cap-pth-small2]
  R1 = Resistor [tolerance=±5% resistance=4.7k package="2512 [SMD]"]
  R2 = Resistor [tolerance=±5% resistance=4.7k package="2512 [SMD]"]
  R3 = Resistor [tolerance=±5% resistance=4.7k package="2512 [SMD]"]
  R4 = Resistor [tolerance=±5% resistance=4.7k package="2512 [SMD]"]
  R5 = Resistor [tolerance=±5% resistance=4.7k package="2512 [SMD]"]
  R7 = Resistor [tolerance=±5% resistance=4.7k package="2512 [SMD]"]
  S1 = SWITCH-MOMENTARY-2 [package=tactile-pth]
  ZS-042_RTC1 = ZS-042 RTC Module
  Q1 = Basic FET N-Channel [package="DPak [SMD]"]
  Q2 = Basic FET N-Channel [package="DPak [SMD]"]
  Part2 = Soil Moisture Sensor
  Part3 = Soil Moisture Sensor
  HC-SR04_Sensor_1 = HC-SR04 Ultrasonic Distance Sensor
  RHT1 = Humidity and Temperature Sensor RHT03
  R8 = Resistor [tolerance=±5% resistance=4.7k package="2512 [SMD]"]
  M1 = DC Motor
  D1 = Diode [package=diode-hv]
  M2 = DC Motor
  D2 = Diode [package=diode-hv]

nets:
  N1: Part1.D0/TX, U3.GPIO_13
  N2: Part1.D1/RX, U3.GPIO_15, R4.Pin_0
  N3: Part1.A4, ZS-042_RTC1.SDA
  N4: Part1.A5, ZS-042_RTC1.SCL
  VCC: Part1.RAW, U2.OUT, U3.VCC, C1.+, C2.1, C3.+, C4.1, R1.Pin_0, R2.Pin_0, R3.Pin_0, S1.1, ZS-042_RTC1.VCC
  GND: Part1.GND, U2.GND, V1.V-, U3.GND, C1.-, C2.2, C3.-, C4.2, R4.Pin_1, R5.Pin_1, R7.Pin_1, ZS-042_RTC1.GND, Q1.source, Q2.source, Part2.GND, Part3.GND, HC-SR04_Sensor_1.ECHO, RHT1.GND_2
  N5: Part1.A1, Part3.SIG
  N6: Part1.A0, Part2.SIG
  N7: Part1.D13/SCK, HC-SR04_Sensor_1.TRIG
  N8: Part1.D12/MISO, HC-SR04_Sensor_1.GND
  N9: Part1.D11_PWM/MOSI, RHT1.Data-signal, R8.Pin_1
  VCC_2: Part1.D10_PWM/SS, Part2.VCC, Part3.VCC, HC-SR04_Sensor_1.VCC, RHT1.Vcc, R8.Pin_0
  N10: Part1.D9_PWM, Q2.Gate
  N11: Part1.D8, Q1.Gate
  N12: Part1.D4, U3.REST, R3.Pin_1
  N13: Part1.D3_PWM, U3.GPIO_14, R5.Pin_0
  N14: Part1.D2, ZS-042_RTC1.SQW
  N15: U2.IN, V1.V+, M1.pin_1, D1.C, M2.pin_1, D2.C
  N16: U3.GPIO_0, R2.Pin_1
  N17: U3.CH_PD, R1.Pin_1
  N18: U3.GPIO_5, R7.Pin_0, S1.2
  N19: Q1.drain, M2.pin_2, D2.A
  N20: Q2.drain, M1.pin_2, D1.A
